// Logisim project game_of_life.circ as structural Verilog: 2 circuits, main circuit main
module game_of_life_cell (
  input  D,
  input  CLK,
  input  RST,
  input  NW,
  input  N,
  input  NE,
  input  W,
  input  E,
  input  SW,
  input  S,
  input  SE,
  output out_12
);

  wire and_1_out, comparator_1_eq, comparator_2_eq, register_1_q;
  wire [3:0] bitadder_1_out;

  Register #(.width(1)) register_1 (.D(D), .clk(CLK), .Q(register_1_q), .clr(RST));  // open: en
  BitAdder bitadder_1 (.in0({SE, S, SW, E, W, NE, N, NW}), .out(bitadder_1_out));
  Comparator #(.width(4)) comparator_1 (.a(bitadder_1_out), .b(4'b0010), .eq(comparator_1_eq));  // open: gt, lt
  Comparator #(.width(4)) comparator_2 (.a(bitadder_1_out), .b(4'b0011), .eq(comparator_2_eq));  // open: gt, lt
  and and_1 (and_1_out, register_1_q, comparator_1_eq);
  or or_1 (out_12, and_1_out, comparator_2_eq);

  // Other names for the same wires on the sheet: next_state = out_12
endmodule

module main (
  input  RESET
);

  wire clock_1_out;

  Clock clock_1 (.out(clock_1_out));
  game_of_life_cell game_of_life_cell_1 (
    .CLK(clock_1_out), .RST(RESET));  // open: D, NW, N, NE, W, E, SW, S, SE, out_12
  game_of_life_cell game_of_life_cell_2 (
    .CLK(clock_1_out), .RST(RESET));  // open: D, NW, N, NE, W, E, SW, S, SE, out_12
  game_of_life_cell game_of_life_cell_3 (
    .CLK(clock_1_out), .RST(RESET));  // open: D, NW, N, NE, W, E, SW, S, SE, out_12
  game_of_life_cell game_of_life_cell_4 (
    .CLK(clock_1_out), .RST(RESET));  // open: D, NW, N, NE, W, E, SW, S, SE, out_12
  game_of_life_cell game_of_life_cell_5 (
    .CLK(clock_1_out), .RST(RESET));  // open: D, NW, N, NE, W, E, SW, S, SE, out_12
  game_of_life_cell game_of_life_cell_6 (.CLK(clock_1_out));  // open: D, RST, NW, N, NE, W, E, SW, S, SE, out_12
  game_of_life_cell game_of_life_cell_7 (
    .CLK(clock_1_out), .RST(RESET));  // open: D, NW, N, NE, W, E, SW, S, SE, out_12
  game_of_life_cell game_of_life_cell_8 (
    .CLK(clock_1_out), .RST(RESET));  // open: D, NW, N, NE, W, E, SW, S, SE, out_12
  game_of_life_cell game_of_life_cell_9 (
    .CLK(clock_1_out), .RST(RESET));  // open: D, NW, N, NE, W, E, SW, S, SE, out_12
  game_of_life_cell game_of_life_cell_10 (
    .CLK(clock_1_out), .RST(RESET));  // open: D, NW, N, NE, W, E, SW, S, SE, out_12
  game_of_life_cell game_of_life_cell_11 (.CLK(clock_1_out));  // open: D, RST, NW, N, NE, W, E, SW, S, SE, out_12
  game_of_life_cell game_of_life_cell_12 (
    .CLK(clock_1_out), .RST(RESET));  // open: D, NW, N, NE, W, E, SW, S, SE, out_12
  game_of_life_cell game_of_life_cell_13 (
    .CLK(clock_1_out), .RST(RESET));  // open: D, NW, N, NE, W, E, SW, S, SE, out_12
  game_of_life_cell game_of_life_cell_14 (
    .CLK(clock_1_out), .RST(RESET));  // open: D, NW, N, NE, W, E, SW, S, SE, out_12
  game_of_life_cell game_of_life_cell_15 (
    .CLK(clock_1_out), .RST(RESET));  // open: D, NW, N, NE, W, E, SW, S, SE, out_12
  game_of_life_cell game_of_life_cell_16 (
    .CLK(clock_1_out), .RST(RESET));  // open: D, NW, N, NE, W, E, SW, S, SE, out_12
endmodule
